# Fritzing sketch taupunktluefterEinfach (saved by Fritzing 0.9.3b)
breadboards: 1

parts:
  Bauteil1 = Arduino Nano (Rev3.0)
  R1 = Resistor [tolerance=±5% resistance=10k package=THT]
  R2 = Resistor [tolerance=±5% resistance=10k package=THT]
  DHT22 = Humidity and Temperature Sensor RHT03
  DHT22_2 = Humidity and Temperature Sensor RHT03
  LED1 = LED - 5mm [color="Red (633nm)" package="5 mm [THT]"]
  LED2 = LED - 5mm [color="Green (560nm)" package="5 mm [THT]"]
  R3 = Resistor [tolerance=±5% resistance=330 package=THT]
  Relais_Module = mystery part, 3 pins [chip_label=?]

nets:
  N1: Bauteil1.GND, DHT22.GND_1, DHT22_2.GND_1, R3.Pin_0, Relais_Module.pin1
  N2: Bauteil1.D4, R1.Pin_1, DHT22.Data-signal
  N3: Bauteil1.D5, R2.Pin_1, DHT22_2.Data-signal
  N4: Bauteil1.D6, Relais_Module.pin2
  N5: Bauteil1.D11/MOSI, LED2.anode
  N6: Bauteil1.D12/MISO, LED1.anode
  VCC: Bauteil1.5V, R1.Pin_0, R2.Pin_0, DHT22.Vcc, DHT22_2.Vcc, Relais_Module.pin3
  N7: LED1.cathode, LED2.cathode, R3.Pin_1

notes:
  Relais Modul
  230 V Seite hier nicht eingezeichnet
